// Digital circuit demux8.dig as structural Verilog
module demux8 (
  input  M,
  input  S0,
  input  S1,
  input  S2,
  output B0,
  output B1,
  output B2,
  output B3,
  output B4,
  output B5,
  output B6,
  output B7
);

  and and_1 (B0, M, ~S0, ~S1, ~S2);  // And
  and and_2 (B1, M, ~S0, ~S1, S2);  // And
  and and_3 (B2, M, ~S0, S1, ~S2);  // And
  and and_4 (B3, M, ~S0, S1, S2);  // And
  and and_5 (B4, M, S0, ~S1, ~S2);  // And
  and and_6 (B5, M, S0, ~S1, S2);  // And
  and and_7 (B6, M, S0, S1, ~S2);  // And
  and and_8 (B7, M, S0, S1, S2);
endmodule
