// Digital circuit mux4.dig as structural Verilog
module mux4 (
  input  A0,
  input  A1,
  input  A2,
  input  A3,
  input  S0,
  input  S1,
  output O
);

  wire and_1_out, and_2_out, and_3_out, and_4_out;

  and and_1 (and_1_out, A0, ~S0, ~S1);  // And
  and and_2 (and_2_out, A1, ~S0, S1);  // And
  and and_3 (and_3_out, A2, S0, ~S1);  // And
  and and_4 (and_4_out, A3, S0, S1);
  or or_1 (O, and_1_out, and_2_out, and_3_out, and_4_out);
endmodule
