// Digital circuit portas.dig as structural Verilog
module portas (
  input  A2,
  input  B2,
  input  B0,
  input  B1,
  input  A0,
  input  A1,
  output M
);

  wire prep_1_m, xnor_1_out;

  xnor xnor_1 (xnor_1_out, A2, B2);
  prep prep_1 (.B0(B0), .B1(B1), .A0(A0), .A1(A1), .M(prep_1_m));
  // mux2 mux2_1: pin names not known; wires that end beside it: A2, prep_1_m, xnor_1_out, M
endmodule
