// Digital circuit prep.dig as structural Verilog
module prep (
  input  B0,
  input  B1,
  input  A0,
  input  A1,
  output M
);

  wire and_1_out, and_2_out, and_3_out, and_4_out, and_5_out, and_6_out, xor_1_out, xor_2_out;

  xor xor_1 (xor_1_out, A1, A0);
  and and_1 (and_1_out, A1, A0);
  xor xor_2 (xor_2_out, B1, B0);
  and and_2 (and_2_out, ~B1, ~B0);  // And
  and and_3 (and_3_out, and_2_out, xor_1_out);
  and and_4 (and_4_out, and_1_out, xor_2_out);
  and and_5 (and_5_out, A1, A0, ~B1, ~B0);  // And
  and and_6 (and_6_out, A1, ~A0, ~B1, B0);  // And
  or or_1 (M, and_3_out, and_4_out, and_5_out, and_6_out);
endmodule
