// Digital circuit primomult.dig as structural Verilog
module primomult (
  input  A0,
  input  A1,
  input  A2,
  input  A3,
  output P,
  output D
);

  wire and_1_out, and_2_out, and_3_out, and_4_out, and_5_out, and_6_out, or_1_out, or_2_out, or_3_out,
       or_4_out, xor_1_out;

  and and_1 (and_1_out, ~A3, ~A2, A1);  // And
  and and_2 (and_2_out, ~A1, A2, A0);  // And
  xor xor_1 (xor_1_out, A2, A3);
  or or_1 (or_1_out, A3, ~A2);  // Or
  or or_2 (or_2_out, A2, ~A3);  // Or
  or or_3 (or_3_out, A1, ~A0);  // Or
  or or_4 (or_4_out, A0, ~A1);  // Or
  and and_3 (and_3_out, ~A3, A2, A1, ~A0);  // And
  and and_4 (and_4_out, ~A2, A3, A0, ~A1);  // And
  and and_5 (and_5_out, A0, A1, xor_1_out);
  and and_6 (and_6_out, or_1_out, or_2_out, or_3_out, or_4_out);
  or or_5 (P, and_1_out, and_2_out, and_5_out);
  or or_6 (D, and_6_out, and_3_out, and_4_out);
endmodule
