// Digital circuit serial.dig as structural Verilog
module serial (
  input  A0,
  input  A1,
  input  A2,
  input  A3,
  input  A4,
  input  A5,
  input  A6,
  input  A7,
  input  S0,
  input  S1,
  input  S2
);

  wire demux8_1_b0, demux8_1_b1, demux8_1_b2, demux8_1_b3, demux8_1_b4, demux8_1_b5, demux8_1_b6,
       demux8_1_b7, mux8_1_m;

  mux8 mux8_1 (
    .A0(A0), .A1(A1), .A2(A2), .A3(A3), .A4(A4), .A5(A5), .A6(A6), .A7(A7), .S2(S0), .S0(S2), .S1(S1),
    .M(mux8_1_m));
  demux8 demux8_1 (
    .M(mux8_1_m), .S0(S0), .S1(S1), .S2(S2), .B0(demux8_1_b0), .B1(demux8_1_b1), .B2(demux8_1_b2),
    .B3(demux8_1_b3), .B4(demux8_1_b4), .B5(demux8_1_b5), .B6(demux8_1_b6), .B7(demux8_1_b7));
  LED LED0 (.in(demux8_1_b0));
  LED LED1 (.in(demux8_1_b1));
  LED LED2 (.in(demux8_1_b2));
  LED LED3 (.in(demux8_1_b3));
  LED LED4 (.in(demux8_1_b4));
  LED LED5 (.in(demux8_1_b5));
  LED LED6 (.in(demux8_1_b6));
  LED LED7 (.in(demux8_1_b7));
endmodule
