// Digital circuit ULA16.dig as structural Verilog
module ULA16 (
  input  B15,
  input  B13,
  input  B12,
  input  B11,
  input  B10,
  input  B9,
  input  B8,
  input  B7,
  input  B6,
  input  B5,
  input  B4,
  input  B3,
  input  B2,
  input  B1,
  input  B0,
  input  S2,
  input  S1,
  input  S0,
  input  A15,
  input  A14,
  input  A13,
  input  A12,
  input  A11,
  input  A10,
  input  A9,
  input  A8,
  input  A7,
  input  A6,
  input  A5,
  input  A4,
  input  A3,
  input  A2,
  input  A1,
  input  A0,
  input  B14,
  output r15,
  output r14,
  output r13,
  output r12,
  output r11,
  output r10,
  output r9,
  output r8,
  output r7,
  output r6,
  output r5,
  output r4,
  output r3,
  output r2,
  output r1,
  output r0,
  output OVF
);

  wire soma16_1__0, soma16_1__1, soma16_1__2, soma16_1__3, soma16_1__4, soma16_1__5, soma16_1__6,
       soma16_1__7, soma16_1__8, soma16_1__9, soma16_1__10, soma16_1__11, soma16_1__12, soma16_1__13,
       soma16_1__14, soma16_1__15;

  ULA ula_1 (.A(A15), .B(B15), .plus(soma16_1__15), .Ai_plus_1(A15), .Ai_1(A14), .S2(S2), .S1(S1), .S0(S0), .r(r15));
  ULA ula_2 (.A(A14), .B(B14), .plus(soma16_1__14), .Ai_plus_1(A15), .Ai_1(A13), .S2(S2), .S1(S1), .S0(S0), .r(r14));
  ULA ula_3 (.A(A13), .B(B13), .plus(soma16_1__13), .Ai_plus_1(A14), .Ai_1(A12), .S2(S2), .S1(S1), .S0(S0), .r(r13));
  ULA ula_4 (.A(A12), .B(B12), .plus(soma16_1__12), .Ai_plus_1(A13), .Ai_1(A11), .S2(S2), .S1(S1), .S0(S0), .r(r12));
  ULA ula_5 (.A(A11), .B(B11), .plus(soma16_1__11), .Ai_plus_1(A12), .Ai_1(A10), .S2(S2), .S1(S1), .S0(S0), .r(r11));
  ULA ula_6 (.A(A10), .B(B10), .plus(soma16_1__10), .Ai_plus_1(A11), .Ai_1(A9), .S2(S2), .S1(S1), .S0(S0), .r(r10));
  ULA ula_7 (.A(A9), .B(B9), .plus(soma16_1__9), .Ai_plus_1(A10), .Ai_1(A8), .S2(S2), .S1(S1), .S0(S0), .r(r9));
  soma16 soma16_1 (
    .A7(A7), .A6(A6), .A5(A5), .A4(A4), .A3(A3), .A2(A2), .A1(A1), .A0(A0), .B7(B7), .B6(B6), .B5(B5),
    .B4(B4), .B3(B3), .B2(B2), .B1(B1), .B0(B0), .A15(A15), .A14(A14), .A13(A13), .A12(A12), .A11(A11),
    .A10(A10), .A9(A9), .A8(A8), .B15(B15), .B14(B14), .B13(B13), .B12(B12), .B11(B11), .B10(B10), .B9(B9),
    .B8(B8), .Inv(S0), ._7(soma16_1__7), ._6(soma16_1__6), ._5(soma16_1__5), ._4(soma16_1__4),
    ._0(soma16_1__0), ._1(soma16_1__1), ._2(soma16_1__2), ._3(soma16_1__3), ._15(soma16_1__15),
    ._14(soma16_1__14), ._13(soma16_1__13), ._12(soma16_1__12), ._8(soma16_1__8), ._9(soma16_1__9),
    ._10(soma16_1__10), ._11(soma16_1__11), .O(OVF));
  ULA ula_8 (.A(A8), .B(B8), .plus(soma16_1__8), .Ai_plus_1(A9), .Ai_1(A7), .S2(S2), .S1(S1), .S0(S0), .r(r8));
  ULA ula_9 (.A(A7), .B(B7), .plus(soma16_1__7), .Ai_plus_1(A8), .Ai_1(A6), .S2(S2), .S1(S1), .S0(S0), .r(r7));
  ULA ula_10 (.A(A6), .B(B6), .plus(soma16_1__6), .Ai_plus_1(A7), .Ai_1(A5), .S2(S2), .S1(S1), .S0(S0), .r(r6));
  ULA ula_11 (.A(A5), .B(B5), .plus(soma16_1__5), .Ai_plus_1(A6), .Ai_1(A4), .S2(S2), .S1(S1), .S0(S0), .r(r5));
  ULA ula_12 (.A(A4), .B(B4), .plus(soma16_1__4), .Ai_plus_1(A5), .Ai_1(A3), .S2(S2), .S1(S1), .S0(S0), .r(r4));
  ULA ula_13 (.A(A3), .B(B3), .plus(soma16_1__3), .Ai_plus_1(A4), .Ai_1(A2), .S2(S2), .S1(S1), .S0(S0), .r(r3));
  ULA ula_14 (.A(A2), .B(B2), .plus(soma16_1__2), .Ai_plus_1(A3), .Ai_1(A1), .S2(S2), .S1(S1), .S0(S0), .r(r2));
  ULA ula_15 (.A(A1), .B(B1), .plus(soma16_1__1), .Ai_plus_1(A2), .Ai_1(A0), .S2(S2), .S1(S1), .S0(S0), .r(r1));
  ULA ula_16 (.A(A0), .B(B0), .plus(soma16_1__0), .Ai_plus_1(A1), .Ai_1(1'b0), .S2(S2), .S1(S1), .S0(S0), .r(r0));
endmodule
