// Digital circuit ULAsimples16.dig as structural Verilog
module ULAsimples16 (
  input  B15,
  input  B13,
  input  B12,
  input  B11,
  input  B10,
  input  B9,
  input  B8,
  input  B7,
  input  B6,
  input  B5,
  input  B4,
  input  B3,
  input  B2,
  input  B1,
  input  B0,
  input  B14,
  input  A15,
  input  A13,
  input  A12,
  input  A11,
  input  A10,
  input  A9,
  input  A8,
  input  A7,
  input  A6,
  input  A5,
  input  A4,
  input  A3,
  input  A2,
  input  A1,
  input  A0,
  input  A14,
  input  S2,
  input  S1,
  input  S0,
  output out_36,
  output out_37,
  output out_38,
  output out_39,
  output out_40,
  output out_41,
  output out_42,
  output out_43,
  output out_44,
  output out_45,
  output out_46,
  output out_47,
  output out_48,
  output out_49,
  output out_50,
  output out_51,
  output out_52
);

  ULA16 ula16_1 (
    .B15(B15), .B13(B13), .B12(B12), .B11(B11), .B10(B10), .B9(B9), .B8(B8), .B7(B7), .B6(B6), .B5(B5),
    .B4(B4), .B3(B3), .B2(B2), .B1(B1), .B0(B0), .S2(S2), .S1(S1), .S0(S0), .A15(A15), .A14(A14), .A13(A13),
    .A12(A12), .A11(A11), .A10(A10), .A9(A9), .A8(A8), .A7(A7), .A6(A6), .A5(A5), .A4(A4), .A3(A3), .A2(A2),
    .A1(A1), .A0(A0), .B14(B14), .r15(out_46), .r14(out_45), .r13(out_44), .r12(out_47), .r11(out_42),
    .r10(out_41), .r9(out_40), .r8(out_43), .r7(out_38), .r6(out_37), .r5(out_36), .r4(out_39), .r3(out_50),
    .r2(out_49), .r1(out_48), .r0(out_51), .OVF(out_52));
endmodule
