// Digital circuit mux2.dig as structural Verilog
module mux2 (
  input  B,
  input  i,
  output Z
);

  wire and_1_out, and_2_out;

  and and_1 (and_1_out, B, ~i);  // And
  and and_2 (and_2_out, ~B, i);  // And
  or or_1 (Z, and_1_out, and_2_out);
endmodule
