// Digital circuit mux8.dig as structural Verilog
module mux8 (
  input  A0,
  input  A1,
  input  A2,
  input  A3,
  input  A4,
  input  A5,
  input  A6,
  input  A7,
  input  S2,
  input  S0,
  input  S1,
  output M
);

  wire and_1_out, and_2_out, and_3_out, and_4_out, and_5_out, and_6_out, and_7_out, and_8_out;

  and and_1 (and_1_out, A0, ~S2, ~S1, ~S0);  // And
  and and_2 (and_2_out, A1, ~S2, ~S1, S0);  // And
  and and_3 (and_3_out, A2, ~S2, S1, ~S0);  // And
  and and_4 (and_4_out, A3, ~S2, S1, S0);  // And
  and and_5 (and_5_out, A4, S2, ~S1, ~S0);  // And
  and and_6 (and_6_out, A5, S2, ~S1, S0);  // And
  and and_7 (and_7_out, A6, S2, S1, ~S0);  // And
  and and_8 (and_8_out, A7, S2, S1, S0);
  or or_1 (M, and_1_out, and_2_out, and_3_out, and_4_out, and_5_out, and_6_out, and_7_out, and_8_out);
endmodule
