// Digital circuit soma1.dig as structural Verilog
module soma1 (
  input  A,
  input  B,
  input  v_2,
  input  I,
  output S,
  output V
);

  wire and_1_out, and_2_out, and_3_out, mux2_1_z;

  mux2 mux2_1 (.B(B), .i(I), .Z(mux2_1_z));
  xor xor_1 (S, v_2, mux2_1_z, A);
  and and_1 (and_1_out, A, mux2_1_z);
  and and_2 (and_2_out, A, v_2);
  and and_3 (and_3_out, mux2_1_z, v_2);
  or or_1 (V, and_1_out, and_2_out, and_3_out);
endmodule
