// Digital circuit soma4.dig as structural Verilog
module soma4 (
  input  I,
  input  A0,
  input  B0,
  input  A1,
  input  B1,
  input  A2,
  input  B2,
  input  A3,
  input  B3,
  input  v_2,
  output S0,
  output S1,
  output S2,
  output S3,
  output V
);

  wire soma1_2_v, soma1_3_v, soma1_4_v;

  soma1 soma1_1 (.A(A3), .B(B3), .v_2(soma1_2_v), .I(I), .S(S3), .V(V));
  soma1 soma1_2 (.A(A2), .B(B2), .v_2(soma1_3_v), .I(I), .S(S2), .V(soma1_2_v));
  soma1 soma1_3 (.A(A1), .B(B1), .v_2(soma1_4_v), .I(I), .S(S1), .V(soma1_3_v));
  soma1 soma1_4 (.A(A0), .B(B0), .v_2(v_2), .I(I), .S(S0), .V(soma1_4_v));
endmodule
