// Digital circuit soma8.dig as structural Verilog
module soma8 (
  input  A3,
  input  A2,
  input  A1,
  input  A0,
  input  B3,
  input  B2,
  input  B1,
  input  B0,
  input  I,
  input  A7,
  input  A6,
  input  A5,
  input  A4,
  input  B7,
  input  B6,
  input  B5,
  input  B4,
  input  v,
  output S7,
  output S6,
  output S5,
  output S4,
  output S0,
  output S1,
  output S2,
  output S3,
  output VU
);

  wire or_1_out, soma4_1_s0, soma4_1_s1, soma4_1_s2, soma4_1_s3, soma4_1_v, soma4_2_s0, soma4_2_s1,
       soma4_2_s2, soma4_2_s3, soma4_2_v, soma4_3_v;

  or or_1 (or_1_out, soma4_2_v, soma4_3_v);
  and and_1 (VU, soma4_1_v, or_1_out);
  mux2NORMAL mux2normal_1 (.E0(soma4_2_s3), .E1(soma4_1_s3), .S(soma4_3_v), .M(S7));
  mux2NORMAL mux2normal_2 (.E0(soma4_2_s2), .E1(soma4_1_s2), .S(soma4_3_v), .M(S6));
  soma4 soma4_1 (
    .I(I), .A0(A4), .B0(B4), .A1(A5), .B1(B5), .A2(A6), .B2(B6), .A3(A7), .B3(B7), .v_2(1'b1),
    .S0(soma4_1_s0), .S1(soma4_1_s1), .S2(soma4_1_s2), .S3(soma4_1_s3), .V(soma4_1_v));
  mux2NORMAL mux2normal_3 (.E0(soma4_2_s1), .E1(soma4_1_s1), .S(soma4_3_v), .M(S5));
  mux2NORMAL mux2normal_4 (.E0(soma4_2_s0), .E1(soma4_1_s0), .S(soma4_3_v), .M(S4));
  soma4 soma4_2 (
    .I(I), .A0(A4), .B0(B4), .A1(A5), .B1(B5), .A2(A6), .B2(B6), .A3(A7), .B3(B7), .v_2(1'b0),
    .S0(soma4_2_s0), .S1(soma4_2_s1), .S2(soma4_2_s2), .S3(soma4_2_s3), .V(soma4_2_v));
  soma4 soma4_3 (
    .I(I), .A0(A0), .B0(B0), .A1(A1), .B1(B1), .A2(A2), .B2(B2), .A3(A3), .B3(B3), .v_2(v), .S0(S0), .S1(S1),
    .S2(S2), .S3(S3), .V(soma4_3_v));
endmodule
