// Digital circuit fatControle.dig as structural Verilog
module fatControle (
  input  START,
  input  CLK,
  input  [3:0] N,
  output DONE,
  output [31:0] F
);

  wire \end , l;
  wire [3:2] register_2_q, rom_1_d;

  Register register_1 (.D(rom_1_d[2]), .C(CLK), .en(1'b1), .Q(register_2_q[2]));
  Register register_2 (.D(rom_1_d[3]), .C(CLK), .en(1'b1), .Q(register_2_q[3]));
  fatDatapath fatdatapath_1 (.CLK(CLK), .LD(l), .N(N), .STOP(DONE), .F(F), .END(\end ));
  ROM #(.AddrBits(4), .Bits(4)) rom_1 (.A({register_2_q, START, \end }), .sel(1'b1), .D({rom_1_d, l, DONE}));
  LED led_1 (.in(DONE));

  // Other names for the same wires on the sheet: c = CLK; st = START

  // Notes on the sheet:
  //   contents of rom_1 (hex, n*v repeats v):
  //   2,2,6,6,4,8,4,8,1,1,9,9
endmodule

/* Test case:
CLK  START   N   F            DONE
C     0      5   0x00000001     0
C     1      5   0x00000001     0
C     1      5   0x00000005     0
C     1      5   0x00000014     0
C     1      5   0x0000003C     0
C     1      5   0x00000078     0
C     1      5   0x00000078     1
C     1      5   0x00000078     1
C     1      5   0x00000078     1
C     0      12  0x00000078     0
C     1      12  0x00000001     0
C     1      12  0x0000000C     0
C     1      12  0x00000084     0
C     1      12  0x00000528     0
C     1      12  0x00002E68     0
C     1      12  0x00017340     0
C     1      12  0x000A26C0     0
C     1      12  0x003CE880     0
C     1      12  0x01308A80     0
C     1      12  0x04C22A00     0
C     1      12  0x0E467E00     0
C     1      12  0x1C8CFC00     0
C     1      12  0x1C8CFC00     1
C     1      12  0x1C8CFC00     1
C     1      12  0x1C8CFC00     1
C     1      12  0x1C8CFC00     1
*/
