// Digital circuit fatDatapath.dig as structural Verilog
module fatDatapath (
  input  CLK,
  input  LD,
  input  [3:0] N,
  input  STOP,
  output [31:0] F,
  output END
);

  wire nor_1_out, or_1_out;
  wire [3:0] multiplexer_1_out, register_1_q, sub_1_s;
  wire [31:0] multiplexer_2_out, register_2_q;
  wire [63:0] mul_1_mul;

  nor nor_1 (nor_1_out, N[0], N[1], N[2], N[3]);
  Multiplexer #(.Bits(4)) multiplexer_1 (.sel(LD), .in_0(sub_1_s), .in_1(N), .out(multiplexer_1_out));
  Register #(.Bits(4)) register_1 (.D(multiplexer_1_out), .C(CLK), .en(1'b1), .Q(register_1_q));
  Sub #(.Bits(4)) sub_1 (.a(register_1_q), .b(4'b0000), .c_i(1'b1), .s(sub_1_s));  // open: c_o
  Mul #(.Bits(32)) mul_1 (.a({{28{1'b0}}, register_1_q}), .b(F), .mul(mul_1_mul));
  or or_1 (or_1_out, ~register_1_q[0], register_1_q[1], register_1_q[2], register_1_q[3]);  // Or
  not not_1 (END, or_1_out);
  Multiplexer #(.Bits(32)) multiplexer_2 (.sel(LD), .in_0(mul_1_mul[31:0]), .in_1(32'h1), .out(multiplexer_2_out));
  Register #(.Bits(32)) register_2 (.D(multiplexer_2_out), .C(CLK), .en(~STOP), .Q(register_2_q));
  Multiplexer #(.Bits(32)) multiplexer_3 (.sel(nor_1_out), .in_0(register_2_q), .in_1(32'h1), .out(F));

  // Other names for the same wires on the sheet: c = CLK
endmodule

/* Test case:
CLK   LD   N   STOP F     
C     1    0   0    0x00000001	
C     0    0   0    0x00000001
C     1    5   0    0x00000001
C     0    5   0    0x00000005
C     0    5   0    0x00000014
C     0    5   0    0x0000003C
C     0    5   0    0x00000078
C     0    5   1    0x00000078
C     0    5   1    0x00000078
C     1    12  0    0x00000001
C     0    12  0    0x0000000C
C     0    12  0    0x00000084
C     0    12  0    0x00000528
C     0    12  0    0x00002E68
C     0    12  0    0x00017340
C     0    12  0    0x000A26C0
C     0    12  0    0x003CE880
C     0    12  0    0x01308A80
C     0    12  0    0x04C22A00
C     0    12  0    0x0E467E00
C     0    12  0    0x1C8CFC00
C     0    12  1    0x1C8CFC00
C     0    12  1    0x1C8CFC00
*/
