// Digital circuit ULA.dig as structural Verilog
module ULA (
  input  A,
  input  B,
  input  plus,
  input  Ai_plus_1,
  input  Ai_1,
  input  S2,
  input  S1,
  input  S0,
  output r
);

  wire and_1_out, not_1_out, or_1_out, xor_1_out;

  not not_1 (not_1_out, A);
  and and_1 (and_1_out, A, B);
  xor xor_1 (xor_1_out, A, B);
  or or_1 (or_1_out, A, B);
  mux8 mux8_1 (
    .A0(plus), .A1(plus), .A2(Ai_1), .A3(Ai_plus_1), .A4(not_1_out), .A5(and_1_out), .A6(xor_1_out),
    .A7(or_1_out), .S2(S2), .S0(S0), .S1(S1), .M(r));
endmodule
