// Digital circuit ULA16.dig as structural Verilog
module ULA16 (
  input  [2:0] S,
  input  [15:0] A,
  input  [15:0] B,
  output [15:0] r,
  output Z,
  output N,
  output OVF
);

  wire and_1_out, and_2_out, or_2_out, soma16_1__0, soma16_1__1, soma16_1__2, soma16_1__3, soma16_1__4,
       soma16_1__5, soma16_1__6, soma16_1__7, soma16_1__8, soma16_1__9, soma16_1__10, soma16_1__11,
       soma16_1__12, soma16_1__13, soma16_1__14, soma16_1__15, soma16_1_o;

  or or_1 (OVF, and_2_out, and_1_out);
  and and_1 (and_1_out, ~S[2], S[1], ~S[0], A[15]);  // And
  and and_2 (and_2_out, or_2_out, ~S[2], ~S[1], soma16_1_o);  // And
  or or_2 (or_2_out, S[0], ~S[0]);  // Or
  ULA ula_1 (
    .A(A[15]), .B(B[15]), .plus(soma16_1__15), .Ai_plus_1(A[15]), .Ai_1(A[14]), .S2(S[2]), .S1(S[1]),
    .S0(S[0]), .r(N));
  ULA ula_2 (
    .A(A[14]), .B(B[14]), .plus(soma16_1__14), .Ai_plus_1(A[15]), .Ai_1(A[13]), .S2(S[2]), .S1(S[1]),
    .S0(S[0]), .r(r[14]));
  ULA ula_3 (
    .A(A[13]), .B(B[13]), .plus(soma16_1__13), .Ai_plus_1(A[14]), .Ai_1(A[12]), .S2(S[2]), .S1(S[1]),
    .S0(S[0]), .r(r[13]));
  ULA ula_4 (
    .A(A[12]), .B(B[12]), .plus(soma16_1__12), .Ai_plus_1(A[13]), .Ai_1(A[11]), .S2(S[2]), .S1(S[1]),
    .S0(S[0]), .r(r[12]));
  ULA ula_5 (
    .A(A[11]), .B(B[11]), .plus(soma16_1__11), .Ai_plus_1(A[12]), .Ai_1(A[10]), .S2(S[2]), .S1(S[1]),
    .S0(S[0]), .r(r[11]));
  ULA ula_6 (
    .A(A[10]), .B(B[10]), .plus(soma16_1__10), .Ai_plus_1(A[11]), .Ai_1(A[9]), .S2(S[2]), .S1(S[1]),
    .S0(S[0]), .r(r[10]));
  ULA ula_7 (
    .A(A[9]), .B(B[9]), .plus(soma16_1__9), .Ai_plus_1(A[10]), .Ai_1(A[8]), .S2(S[2]), .S1(S[1]), .S0(S[0]),
    .r(r[9]));
  soma16 soma16_1 (
    .A7(A[7]), .A6(A[6]), .A5(A[5]), .A4(A[4]), .A3(A[3]), .A2(A[2]), .A1(A[1]), .A0(A[0]), .B7(B[7]),
    .B6(B[6]), .B5(B[5]), .B4(B[4]), .B3(B[3]), .B2(B[2]), .B1(B[1]), .B0(B[0]), .A15(A[15]), .A14(A[14]),
    .A13(A[13]), .A12(A[12]), .A11(A[11]), .A10(A[10]), .A9(A[9]), .A8(A[8]), .B15(B[15]), .B14(B[14]),
    .B13(B[13]), .B12(B[12]), .B11(B[11]), .B10(B[10]), .B9(B[9]), .B8(B[8]), .Inv(S[0]), ._7(soma16_1__7),
    ._6(soma16_1__6), ._5(soma16_1__5), ._4(soma16_1__4), ._0(soma16_1__0), ._1(soma16_1__1),
    ._2(soma16_1__2), ._3(soma16_1__3), ._15(soma16_1__15), ._14(soma16_1__14), ._13(soma16_1__13),
    ._12(soma16_1__12), ._8(soma16_1__8), ._9(soma16_1__9), ._10(soma16_1__10), ._11(soma16_1__11),
    .O(soma16_1_o));
  ULA ula_8 (
    .A(A[8]), .B(B[8]), .plus(soma16_1__8), .Ai_plus_1(A[9]), .Ai_1(A[7]), .S2(S[2]), .S1(S[1]), .S0(S[0]),
    .r(r[8]));
  ULA ula_9 (
    .A(A[7]), .B(B[7]), .plus(soma16_1__7), .Ai_plus_1(A[8]), .Ai_1(A[6]), .S2(S[2]), .S1(S[1]), .S0(S[0]),
    .r(r[7]));
  ULA ula_10 (
    .A(A[6]), .B(B[6]), .plus(soma16_1__6), .Ai_plus_1(A[7]), .Ai_1(A[5]), .S2(S[2]), .S1(S[1]), .S0(S[0]),
    .r(r[6]));
  ULA ula_11 (
    .A(A[5]), .B(B[5]), .plus(soma16_1__5), .Ai_plus_1(A[6]), .Ai_1(A[4]), .S2(S[2]), .S1(S[1]), .S0(S[0]),
    .r(r[5]));
  nor nor_1 (Z, r[0], r[1], r[2], r[3], r[4], r[5], r[6], r[7], r[8], r[9], r[10], r[11], r[12], r[13], r[14], N);
  ULA ula_12 (
    .A(A[4]), .B(B[4]), .plus(soma16_1__4), .Ai_plus_1(A[5]), .Ai_1(A[3]), .S2(S[2]), .S1(S[1]), .S0(S[0]),
    .r(r[4]));
  ULA ula_13 (
    .A(A[3]), .B(B[3]), .plus(soma16_1__3), .Ai_plus_1(A[4]), .Ai_1(A[2]), .S2(S[2]), .S1(S[1]), .S0(S[0]),
    .r(r[3]));
  ULA ula_14 (
    .A(A[2]), .B(B[2]), .plus(soma16_1__2), .Ai_plus_1(A[3]), .Ai_1(A[1]), .S2(S[2]), .S1(S[1]), .S0(S[0]),
    .r(r[2]));
  ULA ula_15 (
    .A(A[1]), .B(B[1]), .plus(soma16_1__1), .Ai_plus_1(A[2]), .Ai_1(A[0]), .S2(S[2]), .S1(S[1]), .S0(S[0]),
    .r(r[1]));
  ULA ula_16 (
    .A(A[0]), .B(B[0]), .plus(soma16_1__0), .Ai_plus_1(A[1]), .Ai_1(1'b0), .S2(S[2]), .S1(S[1]), .S0(S[0]),
    .r(r[0]));

  assign r[15] = N;
endmodule
