// Digital circuit mux2NORMAL.dig as structural Verilog
module mux2NORMAL (
  input  E0,
  input  E1,
  input  S,
  output M
);

  wire and_1_out, and_2_out;

  and and_1 (and_1_out, E0, ~S);  // And
  and and_2 (and_2_out, E1, S);
  or or_1 (M, and_1_out, and_2_out);
endmodule
