// Digital circuit soma16.dig as structural Verilog
module soma16 (
  input  A7,
  input  A6,
  input  A5,
  input  A4,
  input  A3,
  input  A2,
  input  A1,
  input  A0,
  input  B7,
  input  B6,
  input  B5,
  input  B4,
  input  B3,
  input  B2,
  input  B1,
  input  B0,
  input  A15,
  input  A14,
  input  A13,
  input  A12,
  input  A11,
  input  A10,
  input  A9,
  input  A8,
  input  B15,
  input  B14,
  input  B13,
  input  B12,
  input  B11,
  input  B10,
  input  B9,
  input  B8,
  input  Inv,
  output _7,
  output _6,
  output _5,
  output _4,
  output _0,
  output _1,
  output _2,
  output _3,
  output _15,
  output _14,
  output _13,
  output _12,
  output _8,
  output _9,
  output _10,
  output _11,
  output O
);

  wire and_1_out, not_1_out, or_1_out, soma8_1_s0, soma8_1_s1, soma8_1_s2, soma8_1_s3, soma8_1_s4,
       soma8_1_s5, soma8_1_s6, soma8_1_s7, soma8_1_vu, soma8_2_s0, soma8_2_s1, soma8_2_s2, soma8_2_s3,
       soma8_2_s4, soma8_2_s5, soma8_2_s6, soma8_2_s7, soma8_2_vu, soma8_3_vu;

  or or_1 (or_1_out, soma8_2_vu, soma8_3_vu);
  and and_1 (and_1_out, soma8_1_vu, or_1_out);
  not not_1 (not_1_out, and_1_out);
  mux2NORMAL mux2normal_1 (.E0(and_1_out), .E1(not_1_out), .S(Inv), .M(O));
  mux2NORMAL mux2normal_2 (.E0(soma8_2_s7), .E1(soma8_1_s7), .S(soma8_3_vu), .M(_15));
  mux2NORMAL mux2normal_3 (.E0(soma8_2_s6), .E1(soma8_1_s6), .S(soma8_3_vu), .M(_14));
  mux2NORMAL mux2normal_4 (.E0(soma8_2_s5), .E1(soma8_1_s5), .S(soma8_3_vu), .M(_13));
  soma8 soma8_1 (
    .A3(A11), .A2(A10), .A1(A9), .A0(A8), .B3(B11), .B2(B10), .B1(B9), .B0(B8), .I(Inv), .A7(A15), .A6(A14),
    .A5(A13), .A4(A12), .B7(B15), .B6(B14), .B5(B13), .B4(B12), .v(1'b1), .S7(soma8_1_s7), .S6(soma8_1_s6),
    .S5(soma8_1_s5), .S4(soma8_1_s4), .S0(soma8_1_s0), .S1(soma8_1_s1), .S2(soma8_1_s2), .S3(soma8_1_s3),
    .VU(soma8_1_vu));
  mux2NORMAL mux2normal_5 (.E0(soma8_2_s4), .E1(soma8_1_s4), .S(soma8_3_vu), .M(_12));
  mux2NORMAL mux2normal_6 (.E0(soma8_2_s3), .E1(soma8_1_s3), .S(soma8_3_vu), .M(_11));
  mux2NORMAL mux2normal_7 (.E0(soma8_2_s2), .E1(soma8_1_s2), .S(soma8_3_vu), .M(_10));
  mux2NORMAL mux2normal_8 (.E0(soma8_2_s1), .E1(soma8_1_s1), .S(soma8_3_vu), .M(_9));
  mux2NORMAL mux2normal_9 (.E0(soma8_2_s0), .E1(soma8_1_s0), .S(soma8_3_vu), .M(_8));
  soma8 soma8_2 (
    .A3(A11), .A2(A10), .A1(A9), .A0(A8), .B3(B11), .B2(B10), .B1(B9), .B0(B8), .I(Inv), .A7(A15), .A6(A14),
    .A5(A13), .A4(A12), .B7(B15), .B6(B14), .B5(B13), .B4(B12), .v(1'b0), .S7(soma8_2_s7), .S6(soma8_2_s6),
    .S5(soma8_2_s5), .S4(soma8_2_s4), .S0(soma8_2_s0), .S1(soma8_2_s1), .S2(soma8_2_s2), .S3(soma8_2_s3),
    .VU(soma8_2_vu));
  soma8 soma8_3 (
    .A3(A3), .A2(A2), .A1(A1), .A0(A0), .B3(B3), .B2(B2), .B1(B1), .B0(B0), .I(Inv), .A7(A7), .A6(A6),
    .A5(A5), .A4(A4), .B7(B7), .B6(B6), .B5(B5), .B4(B4), .v(Inv), .S7(_7), .S6(_6), .S5(_5), .S4(_4),
    .S0(_0), .S1(_1), .S2(_2), .S3(_3), .VU(soma8_3_vu));
endmodule
