// Digital circuit trabalho01.dig as structural Verilog
module trabalho01 (
  input  [15:0] B,
  input  [15:0] A,
  input  [2:0] S,
  output OVFL,
  output NEG,
  output ZERO,
  output [15:0] r
);

  ULA16 ula16_1 (.S(S), .A(A), .B(B), .r(r), .Z(ZERO), .N(NEG), .OVF(OVFL));

  // Notes on the sheet:
  //   Funções (S):
  //   0 - Soma
  //   1 - Subtração
  //   2 - <<
  //   3 - >>
  //   4 - Not
  //   5 - And
  //   6 - Xor
  //   7 - Or
endmodule
