// Digital circuit projVetControle.dig as structural Verilog
module projVetControle (
  input  CLK,
  input  START,
  output DONE,
  output [15:0] P
);

  wire clr, fim;
  wire [3:2] register_1_q, rom_1_d;

  Register register_1 (.D(rom_1_d[2]), .C(CLK), .en(1'b1), .Q(register_1_q[2]));
  Register register_2 (.D(rom_1_d[3]), .C(CLK), .en(1'b1), .Q(register_1_q[3]));
  ROM #(.AddrBits(4), .Bits(4)) rom_1 (.A({register_1_q, START, DONE}), .sel(1'b1), .D({rom_1_d, clr, fim}));
  PullUp #(.Bits(4)) pullup_1 (.out({rom_1_d, clr, fim}));
  projVetDataPath projvetdatapath_1 (.CLK(CLK), .CLR(clr), .EN(DONE), .STOP(fim), .P(P), .FIM(DONE));
  LED led_1 (.in(DONE));

  // Other names for the same wires on the sheet: c = CLK; end = DONE; st = START

  // Notes on the sheet:
  //   contents of rom_1 (hex, n*v repeats v):
  //   2,2,6,6,4,8,4,8,1,1,9,9
endmodule

/* Test case:
CLK START  DONE   P
C     0    0      0
C     1    0      2
C     1    0      4
C     1    0      6
C     1    0      8
C     1    0      10
C     1    0      12
C     1    0      14
C     1    1      16
C     1    1      16
C     1    1      16
C     1    1      16
C     1    1      16
C     0    0      0
*/
