// Digital circuit projVetDataPath.dig as structural Verilog
module projVetDataPath (
  input  CLK,
  input  CLR,
  input  EN,
  input  STOP,
  output [15:0] P,
  output FIM
);

  wire add_1_c_o;
  wire [3:0] counter_1_out, counter_2_out;
  wire [7:0] rom_1_d, rom_2_d;
  wire [15:0] add_1_s, mul_1_mul, register_1_q;

  Counter #(.Bits(4)) counter_1 (.en(EN), .C(CLK), .clr(CLR), .out(counter_1_out));  // open: ovf
  Counter #(.Bits(4)) counter_2 (.en(EN), .C(CLK), .clr(CLR), .out(counter_2_out));  // open: ovf
  ROM #(.AddrBits(4), .Bits(8)) rom_1 (.A(counter_1_out), .sel(1'b1), .D(rom_1_d));
  ROM #(.AddrBits(4), .Bits(8)) rom_2 (.A(counter_2_out), .sel(1'b1), .D(rom_2_d));
  Mul #(.Bits(8)) mul_1 (.a(rom_1_d), .b(rom_2_d), .mul(mul_1_mul));
  nor nor_1 (FIM, counter_2_out[0], counter_2_out[1], counter_2_out[2], ~counter_2_out[3]);  // NOr
  Add #(.Bits(16)) add_1 (.a(register_1_q), .b(mul_1_mul), .c_i(add_1_c_o), .s(add_1_s), .c_o(add_1_c_o));
  Register #(.Bits(16)) register_1 (.D(add_1_s), .C(CLK), .en(~STOP), .Q(register_1_q));
  Multiplexer #(.Bits(16)) multiplexer_1 (.sel(CLR), .in_0(register_1_q), .in_1({16{1'b0}}), .out(P));

  // Other names for the same wires on the sheet: c = CLK

  // Notes on the sheet:
  //   contents of rom_1 (hex, n*v repeats v):
  //   1,2,1,2,1,2,1,2,1,2
  //   contents of rom_2 (hex, n*v repeats v):
  //   2,1,2,1,2,1,2,1,2,1
endmodule

/* Test case:
CLK   CLR  EN  STOP P
C     1    0   1    0
C     0    1   0    2
C     0    1   0    4
C     0    1   0    6
C     0    1   0    8
C     0    1   0    10
C     0    1   0    12
C     0    1   0    14
C     0    1   0    16
C     0    1   0    18
C     0    1   0    20
C     0    0   1    20
C     0    0   1    20
C     1    0   1    0
*/
